# Fritzing sketch 01-lipo-charger (saved by Fritzing 1.0.1rc)

parts:
  A1 = mini560 [package=THT]
  part = TP4056 [part_number=TP4056]
  U1 = LIPO-2000mAh [package=lipo-2000]
  part_2 = Resistor [tolerance=±5% power=0.25 resistance=220 package=THT]
  part_3 = LED - 5mm [color="Red (633nm)" current=0.030 package="5 mm [THT]"]

nets:
  N1: A1.pin_1, A1.pin_2, part.pin3
  N2: A1.pin_4, A1.pin_6, A1.pin_7, part.pin6, part_3.cathode
  N3: A1.pin_8, A1.pin_9, part_2.Pin_0
  N4: part.pin4, U1.+
  N5: part.pin5, U1.-
  N6: part_2.Pin_1, part_3.anode

notes:
  Basic LiPo Charger

custom parts:
  mini560: 5A DC-DC Mini 560 Step Down Stabilized Voltage Supply Module Output 3.3 5V 9V 12V Step-down Power Converter Board Module
  TP4056: TP4056 Lithium battery charger / protection module. (this one has the pins on .1 boundaried unlike the original)
